# Fritzing sketch HC05-Nanosin (saved by Fritzing 0.9.3b)

parts:
  Componente1 = Arduino Nano (Rev3.0)
  Componente2 = Bluetooth HC-05 Macho

nets:
  N1: Componente1.D8, Componente2.VCC
  N2: Componente1.D9, Componente2.Key
  N3: Componente1.D10, Componente2.TXD
  N4: Componente1.D11/MOSI, Componente2.RXD
  GND: Componente1.GND, Componente2.GND
