# Fritzing sketch HC06-Nano (saved by Fritzing 0.9.3b)

parts:
  Componente1 = Arduino Nano (Rev3.0)
  Componente2 = Bluetooth HC-05 Macho

nets:
  N1: Componente1.D10, Componente2.TXD
  N2: Componente1.D11/MOSI, Componente2.RXD
  GND: Componente1.GND, Componente2.GND
  5V: Componente1.5V, Componente2.VCC
